# Fritzing sketch pedometer (saved by Fritzing 0.9.3b)

parts:
  부품1 = Arduino Nano (Rev3.0)  # not connected
  U3 = LIPO-110mAh [package=lipo-110]
  kProject_LED_DAC_Board_Rev_1 = kProject LED DAC Board Rev.0
  J1 = Generic female header - 8 pins [form="♀ (female)" package=THT]  # not connected

nets:
  N1: U3.+, kProject_LED_DAC_Board_Rev_1.VCC
  N2: U3.-, kProject_LED_DAC_Board_Rev_1.GND

custom parts:
  Generic female header - 8 pins: Generic female header
